# Fritzing sketch wiring-16-fs3-bench (saved by Fritzing 1.0.0)

parts:
  Board = Unexpected Maker FeatherS3D
  Pi = Testbench Pi the slot's GPIO pair
  D1 = Schottky diode 1N5711
  D2 = Schottky diode 1N5711

nets:
  N1: Board.RST, D1.A
  N2: Board.IO0, D2.A
  GND: Board.GND, Pi.GND
  N3: Pi.EN_(gpio_en), D1.K
  N4: Pi.BOOT_(gpio_boot), D2.K

notes:
  FeatherS3D: the bench's BOOT and RST lines (FSD C-40.9)
  On the board's long header: RST is the first pin (beside 3V3.1), GPIO 0 the third
  (marked 0, the BOOT button's line), GND the fourth (white square). No wire to 3V3.1.
  D1, D2: 1N5711 (or BAT43) Schottky, band (cathode) at the Pi. Pi low pulls the pin
  to about 0.4 V; Pi high is blocked, so the board's pull-up holds the pin and the Pi
  never powers the board. Pi pairs: 1 BCM 17/18 (pins 11/12), 2 BCM 22/23 (15/16),
  3 BCM 24/25 (18/22), 4 BCM 26/27 (37/13); GND pin 14. Then run the BOOT/EN test.
  Title bars: green = firmware on main; blue = in the FSD, not built yet; orange = proposed, not in the FSD.

custom parts:
  Unexpected Maker FeatherS3D: Unexpected Maker FeatherS3D (ESP32-S3), the pins this project uses grouped by use, with both STEMMA QT sockets; not the physical header order.
  Testbench Pi the slot's GPIO pair: The testbench Pi's EN and BOOT GPIOs for the slot (harness manual, GPIO pairs)
