# Fritzing sketch wiring-4-rs232 (saved by Fritzing 1.0.0)

parts:
  Board = LilyGO T-Display-S3 AMOLED 1.91
  U12 = RS232 transceiver MAX3232 (PDIP-16)
  J1 = DE-9 male (DTE)
  R10 = Resistor 100k

nets:
  N1: Board.IO11, U12.T1IN
  N2: Board.IO12, U12.R1OUT
  N3: Board.IO13, U12.VCC, R10.1
  GND: Board.GND, U12.GND, J1.5_GND, R10.2
  N4: U12.T1OUT, J1.3_TXD
  N5: U12.R1IN, J1.2_RXD

notes:
  RS232 instrument (FSD 30) - specified, not built
  UART1: GPIO 11 TX to T1IN, GPIO 12 RX from R1OUT. GPIO 13 is the
  MAX3232's VCC, so it draws nothing while off; the 100k holds it low
  through sleep and reset. DE-9 male, DTE: pin 3 TXD, pin 2 RXD, pin 5 GND
  (or a 3-pin 5.08 mm terminal). Parts and pinout in rs232-circuit.md.

custom parts:
  LilyGO T-Display-S3 AMOLED 1.91: LilyGO T-Display-S3 AMOLED 1.91 inch (ESP32-S3R8), header pins as on LilyGO's pinout picture, seen from the chip side.
  RS232 transceiver MAX3232 (PDIP-16): RS232 transceiver MAX3232 in a DIP socket
  DE-9 male (DTE): DE-9 male connector, DTE
