# Fritzing sketch wiring-9-blues-sensor-bus (saved by Fritzing 1.0.0)

parts:
  Board = LilyGO T-Display-S3 AMOLED 1.91
  J1 = Qwiic star adapter
  U1 = BME280 Qwiic, 0x76
  U13 = RV-8803 RTC Adafruit 6538, 0x32
  U9 = ADS1115 Qwiic, water 0x48
  U2 = Notecarrier-X + Notecard MBGLW
  BT2 = Notecarrier LiPo

nets:
  GND: Board.Q_GND, J1.GND, U1.GND, U13.GND, U9.GND, U9.ADDR, U2.GND
  3V3: Board.Q_3V3, J1.3V3, U1.3V3, U13.3V3, U9.3V3
  N1: Board.Q_SDA, J1.SDA, U1.SDA, U13.SDA, U9.SDA, U2.SDA
  N2: Board.Q_SCL, J1.SCL, U1.SCL, U13.SCL, U9.SCL, U2.SCL
  N3: U2.BAT-, BT2.-
  N4: U2.BAT+, BT2.+

notes:
  Blues build: the sensor bus, GPIO 43 SDA / 44 SCL at 100 kHz (FSD 2.2, 23, 33, 39)
  The board's Qwiic connector feeds a Qwiic star; each Qwiic board plugs into a port:
  BME280 0x76, RV-8803 RTC 0x32, Notecarrier-X 0x17 (its red 3.3 V wire unconnected,
  its own LiPo). The water probe's Qwiic ADS1115 (0x48, ADDR to GND) chains from the
  RTC's second Qwiic socket; A0/A1 and the probe's boost (VSYS, GPIO 2) are sheet 3.
  The BME280's pull-ups and the Notecard's 10k stay; cut the RTC's and the ADS1115's
  (bus at or above about 2.2 kOhm). The RTC's CR1220 keeps the time while the board
  is unpowered. Plug or unplug only with USB and the battery disconnected.
  Title bars: green = firmware on main; blue = in the FSD, not built yet; orange = proposed, not in the FSD.

custom parts:
  LilyGO T-Display-S3 AMOLED 1.91: LilyGO T-Display-S3 AMOLED 1.91 inch (ESP32-S3R8), header pins as on LilyGO's pinout picture, seen from the chip side.
  Qwiic star adapter: Qwiic star adapter (e.g. SparkFun Qwiic MultiPort): every port on one I2C bus
  BME280 Qwiic, 0x76: BME280 breakout on Qwiic (I2C 0x76)
  RV-8803 RTC Adafruit 6538, 0x32: Adafruit RV-8803 RTC breakout (6538) on STEMMA QT, I2C 0x32, CR1220 backup
  ADS1115 Qwiic, water 0x48: ADS1115 on Qwiic for the water probe, address 0x48
  Notecarrier-X + Notecard MBGLW: Blues Notecarrier-X v1.3 with Notecard Cell+WiFi NOTE-MBGLW v2.5
